// Logisim project Main.circ as structural Verilog: 7 circuits, main circuit main
module main (
  input  PC_Reset,
  input  RF_Reset,
  input  Memory_Reset
);

  wire ALU_Enable, Chip_Sel, clock_1_out, clock_2_out, clock_3_out, Data_DMX_Sel, Decoder_Enable,
       Fetch_Enable, Mem_Address_MUX_Sel, Mem_Read_Write, Memory_Enable, MUXB_Sel, MUXY_Sel, RF_Write;
  wire [4:0] id_1_destination, id_1_source_1, id_1_source_2;
  wire [5:0] Op_Code;
  wire [31:0] alu_1_alu_output, demultiplexer_1_out0, demultiplexer_1_out1, fetch_stage_1_ir,
       fetch_stage_1_pc_address, id_1_immediate_value, memory_1_data, multiplexer_1_out, multiplexer_2_out,
       multiplexer_3_out, rf_1_output_a, rf_1_output_b, RM_q, RY_q;

  ID id_1 (
    .Instruction(fetch_stage_1_ir), .Immediate_Value(id_1_immediate_value), .Source_1(id_1_source_1),
    .Destination(id_1_destination), .Op_Code(Op_Code), .Source_2(id_1_source_2));
  RF rf_1 (
    .Input_Data(RY_q), .RF_clear(RF_Reset), .Address_A(id_1_source_1), .Address_B(id_1_source_2),
    .MUX_Enable(Decoder_Enable), .Address_c(id_1_destination), .RF_write(RF_Write), .Output_B(rf_1_output_b),
    .Output_A(rf_1_output_a));
  Multiplexer #(.width(32)) multiplexer_1 (
    .in0(alu_1_alu_output), .in1(demultiplexer_1_out1), .out(multiplexer_1_out), .sel(MUXY_Sel),
    .en(Memory_Enable));
  Clock clock_1 (.out(clock_1_out));
  Fetch_Stage fetch_stage_1 (
    .PC_Reset(PC_Reset), .PC_Address(fetch_stage_1_pc_address), .IR_Input(demultiplexer_1_out0),
    .IR(fetch_stage_1_ir), .Fetch_Enable(Fetch_Enable));
  Multiplexer #(.width(32), .enable("false")) multiplexer_2 (
    .in0(rf_1_output_b), .in1(id_1_immediate_value), .out(multiplexer_2_out), .sel(MUXB_Sel));
  ALU alu_1 (
    .Op_Code(Op_Code), .Input_A(rf_1_output_a), .Input_B(multiplexer_2_out), .ALU_Output(alu_1_alu_output),
    .ALU_MUX_Enable(ALU_Enable));
  Register #(.width(32), .trigger("falling")) RY (
    .D(multiplexer_1_out), .en(Memory_Enable), .Q(RY_q), .clk(clock_1_out));  // open: clr
  Register #(.width(32)) RM (.D(rf_1_output_b), .en(ALU_Enable), .Q(RM_q), .clk(clock_2_out));  // open: clr
  Clock clock_2 (.out(clock_2_out));
  Multiplexer #(.width(32), .enable("false")) multiplexer_3 (
    .in0(fetch_stage_1_pc_address), .in1(alu_1_alu_output), .out(multiplexer_3_out), .sel(Mem_Address_MUX_Sel));
  Demultiplexer #(.width(32), .enable("false")) demultiplexer_1 (
    .out0(demultiplexer_1_out0), .out1(demultiplexer_1_out1), .in(memory_1_data), .sel(Data_DMX_Sel));
  Clock clock_3 (.out(clock_3_out));
  Memory memory_1 (
    .Memory_Address(multiplexer_3_out), .Memory(RM_q), .Data(memory_1_data), .Mem_Reset(Memory_Reset),
    .clk(clock_3_out), .Mem_Read_Write(Mem_Read_Write), .Chip_Sel(Chip_Sel));
  Control_Unit control_unit_1 (
    .Op_Code_6(Op_Code), .Fetch_Enable(Fetch_Enable), .Decode_Enable(Decoder_Enable),
    .Memory_Address_MUX_Sel(Mem_Address_MUX_Sel), .Data_DMX_Sel(Data_DMX_Sel),
    .Mem_Read_Write(Mem_Read_Write), .ALU_Enable(ALU_Enable), .MUXY_Sel(MUXY_Sel),
    .Memory_Enable(Memory_Enable), .MUXB_Sel(MUXB_Sel), .RF_Write(RF_Write), .Chip_Sel(Chip_Sel));
endmodule

module Control_Unit (
  input  [5:0] Op_Code_6,
  output Fetch_Enable,
  output Chip_Sel,
  output Decode_Enable,
  output ALU_Enable,
  output Memory_Address_MUX_Sel,
  output MUXB_Sel,
  output Data_DMX_Sel,
  output RF_Write,
  output Memory_Enable,
  output Mem_Read_Write,
  output MUXY_Sel
);

  wire and_1_out, clock_1_out, cnt, comparator_6_eq, comparator_8_eq, comparator_9_eq, comparator_10_eq,
       comparator_11_eq, comparator_12_eq, not_1_out, not_2_out, not_3_out, not_4_out, or_2_out, s5;
  wire [2:0] Main_Counter_q;
  wire [3:0] Op_code;

  Counter #(.width(3), .max('h4)) Main_Counter (
    .count(cnt), .Q(Main_Counter_q), .clk(clock_1_out));  // open: load, D, carry, clr
  Clock clock_1 (.out(clock_1_out));
  Comparator #(.width(3)) comparator_1 (.a(Main_Counter_q), .b(3'b000), .eq(Fetch_Enable));  // open: gt, lt
  Comparator #(.width(3)) comparator_2 (.a(Main_Counter_q), .b(3'b001), .eq(Decode_Enable));  // open: gt, lt
  Comparator #(.width(3)) comparator_3 (.a(Main_Counter_q), .b(3'b010), .eq(ALU_Enable));  // open: gt, lt
  Comparator #(.width(3)) comparator_4 (.a(Main_Counter_q), .b(3'b011), .eq(Memory_Enable));  // open: gt, lt
  Comparator #(.width(3)) comparator_5 (.a(Main_Counter_q), .b(3'b100), .eq(s5));  // open: gt, lt
  BitSelector #(.width(6), .group(4)) bitselector_1 (.in(Op_Code_6), .out(Op_code), .sel(1'b0));
  nand nand_1 (cnt, Op_Code_6[2], s5, Op_Code_6[3]);
  Comparator #(.width(4)) comparator_6 (.a(4'b1010), .b(Op_code), .eq(comparator_6_eq));  // open: gt, lt
  Comparator #(.width(4)) comparator_7 (.a(4'b1010), .b(Op_code), .eq(MUXY_Sel));  // open: gt, lt
  or or_1 (MUXB_Sel, Op_Code_6[0], comparator_6_eq);
  Comparator #(.width(4)) comparator_8 (.a(4'b1010), .b(Op_code), .eq(comparator_8_eq));  // open: gt, lt
  or or_2 (or_2_out, comparator_8_eq, comparator_9_eq);
  Comparator #(.width(4)) comparator_9 (.a(Op_code), .b(4'b1011), .eq(comparator_9_eq));  // open: gt, lt
  not not_1 (not_1_out, Fetch_Enable);
  not not_2 (not_2_out, Fetch_Enable);
  Comparator #(.width(4)) comparator_10 (.a(4'b1010), .b(Op_code), .eq(comparator_10_eq));  // open: gt, lt
  not not_3 (not_3_out, comparator_10_eq);
  Comparator #(.width(4)) comparator_11 (.a(Op_code), .b(4'b1011), .eq(comparator_11_eq));  // open: gt, lt
  and and_1 (and_1_out, Memory_Enable, or_2_out);
  and and_2 (Data_DMX_Sel, not_1_out, Memory_Enable);
  and and_3 (Mem_Read_Write, not_2_out, not_3_out, comparator_11_eq);
  or or_3 (Chip_Sel, Fetch_Enable, and_1_out);
  not not_4 (not_4_out, comparator_12_eq);
  Comparator #(.width(4)) comparator_12 (.a(Op_code), .b(4'b1011), .eq(comparator_12_eq));  // open: gt, lt
  and and_4 (RF_Write, s5, not_4_out);

  assign Memory_Address_MUX_Sel = Data_DMX_Sel;

  // Other names for the same wires on the sheet: B0 = Op_Code_6[0]; B1 = Op_Code_6[1]; B2 = Op_Code_6[2];
  //   B3 = Op_Code_6[3]; s1 = Fetch_Enable; s2 = Decode_Enable; s3 = ALU_Enable; s4 = Memory_Enable
endmodule

// Fetch
module Fetch_Stage (
  input  PC_Reset,
  input  [31:0] IR_Input,
  input  Fetch_Enable,
  output [31:0] PC_Address,
  output [31:0] IR
);

  wire clock_1_out;
  wire [31:0] adder_1_out;

  Clock clock_1 (.out(clock_1_out));
  Register #(.width(32), .trigger("falling")) PC (
    .D(adder_1_out), .en(Fetch_Enable), .Q(PC_Address), .clk(clock_1_out), .clr(PC_Reset));
  Adder #(.width(32)) adder_1 (.a(PC_Address), .b(32'h1), .out(adder_1_out));  // open: cin, cout
  Register #(.width(32), .trigger("falling")) u_IR (
    .D(IR_Input), .en(Fetch_Enable), .Q(IR), .clk(clock_1_out));  // open: clr
endmodule

// Register File
module RF (
  input  [31:0] Input_Data,
  input  RF_clear,
  input  [4:0] Address_A,
  input  [4:0] Address_B,
  input  MUX_Enable,
  input  [4:0] Address_c,
  input  RF_write,
  output [31:0] Output_A,
  output [31:0] Output_B
);

  wire R1_clear_t, R1_clk, R1_en, R2_clear_t, R2_en, R3_clear_t, R3_en, R4_clear_t, R4_en, R5_clear_t, R5_en,
       R6_clear_t, R6_en, R7_clear_t, R7_en, R8_clear_t, R8_en, R9_clear_t, R9_en, R10_clear_t, R10_en,
       R11_clear_t, R11_en, R12_clear_t, R12_en, R13_clear_t, R13_en, R14_clear_t, R14_en, R15_clear_t,
       R15_en, R16_clear_t, R16_en, R17_clear_t, R17_en, R18_clear_t, R18_en, R19_clear_t, R19_en,
       R20_clear_t, R20_en, R21_clear_t, R21_en, R22_clear_t, R22_en, R23_clear_t, R23_en, R24_clear_t,
       R24_en, R25_clear_t, R25_en, R26_clear_t, R26_en, R27_clear_t, R27_en, R28_clear_t, R28_en,
       R29_clear_t, R29_en, R30_clear_t, R30_en, R31_clear_t, R31_en, R32_clear_t, R32_en;
  wire [31:0] multiplexer_1_out, multiplexer_2_out, R1_o_p, R2_o_p, R3_o_p, R4_o_p, R5_o_p, R6_o_p, R7_o_p,
       R8_o_p, R9_o_p, R10_o_p, R11_o_p, R12_o_p, R13_o_p, R14_o_p, R15_o_p, R16_o_p, R17_o_p, R18_o_p,
       R19_o_p, R20_o_p, R21_o_p, R22_o_p, R23_o_p, R24_o_p, R25_o_p, R26_o_p, R27_o_p, R28_o_p, R29_o_p,
       R30_o_p, R31_o_p, R32_o_p, undriven;

  Register #(.width(32), .trigger("falling")) register_1 (
    .D(Input_Data), .en(R1_en), .Q(R1_o_p), .clk(R1_clk), .clr(R1_clear_t));
  Register #(.width(32), .trigger("falling")) register_2 (
    .D(Input_Data), .en(R9_en), .Q(R9_o_p), .clk(R1_clk), .clr(R9_clear_t));
  Register #(.width(32), .trigger("falling")) register_3 (
    .D(Input_Data), .en(R17_en), .Q(R17_o_p), .clk(R1_clk), .clr(R17_clear_t));
  Register #(.width(32), .trigger("falling")) register_4 (
    .D(Input_Data), .en(R25_en), .Q(R25_o_p), .clk(R1_clk), .clr(R25_clear_t));
  Register #(.width(32), .trigger("falling")) register_5 (
    .D(Input_Data), .en(R2_en), .Q(R2_o_p), .clk(R1_clk), .clr(R2_clear_t));
  Register #(.width(32), .trigger("falling")) register_6 (
    .D(Input_Data), .en(R10_en), .Q(R10_o_p), .clk(R1_clk), .clr(R10_clear_t));
  Register #(.width(32), .trigger("falling")) register_7 (
    .D(Input_Data), .en(R18_en), .Q(R18_o_p), .clk(R1_clk), .clr(R18_clear_t));
  Register #(.width(32), .trigger("falling")) register_8 (
    .D(Input_Data), .en(R26_en), .Q(R26_o_p), .clk(R1_clk), .clr(R26_clear_t));
  Clock clock_1 (.out(R1_clk));
  Register #(.width(32), .trigger("falling")) RB (
    .D(multiplexer_1_out), .en(MUX_Enable), .Q(Output_B), .clk(R1_clk));  // open: clr
  Register #(.width(32), .trigger("falling")) register_9 (
    .D(Input_Data), .en(R3_en), .Q(R3_o_p), .clk(R1_clk), .clr(R3_clear_t));
  Register #(.width(32), .trigger("falling")) register_10 (
    .D(Input_Data), .en(R11_en), .Q(R11_o_p), .clk(R1_clk), .clr(R11_clear_t));
  Register #(.width(32), .trigger("falling")) register_11 (
    .D(Input_Data), .en(R19_en), .Q(R19_o_p), .clk(R1_clk), .clr(R19_clear_t));
  Register #(.width(32), .trigger("falling")) register_12 (
    .D(Input_Data), .en(R27_en), .Q(R27_o_p), .clk(R1_clk), .clr(R27_clear_t));
  Multiplexer #(.select(5), .width(32)) multiplexer_1 (
    .in0(R1_o_p), .in1(R2_o_p), .in2(R3_o_p), .in3(R4_o_p), .in4(R5_o_p), .in5(R6_o_p), .in6(R7_o_p),
    .in7(R8_o_p), .in8(R9_o_p), .in9(R10_o_p), .in10(R11_o_p), .in11(R12_o_p), .in12(R13_o_p),
    .in13(R14_o_p), .in14(R15_o_p), .in15(R16_o_p), .in16(R17_o_p), .in17(R18_o_p), .in18(R19_o_p),
    .in19(R20_o_p), .in20(R21_o_p), .in21(R22_o_p), .in22(R23_o_p), .in23(R24_o_p), .in24(R25_o_p),
    .in25(R26_o_p), .in26(R27_o_p), .in27(R28_o_p), .in28(R29_o_p), .in29(R30_o_p), .in30(R31_o_p),
    .in31(R32_o_p), .out(multiplexer_1_out), .sel(Address_B), .en(MUX_Enable));
  Register #(.width(32), .trigger("falling")) register_13 (
    .D(Input_Data), .en(R4_en), .Q(R4_o_p), .clk(R1_clk), .clr(R4_clear_t));
  Register #(.width(32), .trigger("falling")) register_14 (
    .D(Input_Data), .en(R12_en), .Q(R12_o_p), .clk(R1_clk), .clr(R12_clear_t));
  Register #(.width(32), .trigger("falling")) register_15 (
    .D(Input_Data), .en(R20_en), .Q(R20_o_p), .clk(R1_clk), .clr(R20_clear_t));
  Register #(.width(32), .trigger("falling")) register_16 (
    .D(Input_Data), .en(R28_en), .Q(R28_o_p), .clk(R1_clk), .clr(R28_clear_t));
  Register #(.width(32), .trigger("falling")) register_17 (
    .D(Input_Data), .en(R5_en), .Q(R5_o_p), .clk(R1_clk), .clr(R5_clear_t));
  Register #(.width(32), .trigger("falling")) register_18 (
    .D(Input_Data), .en(R13_en), .Q(R13_o_p), .clk(R1_clk), .clr(R13_clear_t));
  Register #(.width(32), .trigger("falling")) register_19 (
    .D(Input_Data), .en(R21_en), .Q(R21_o_p), .clk(R1_clk), .clr(R21_clear_t));
  Register #(.width(32), .trigger("falling")) register_20 (
    .D(Input_Data), .en(R29_en), .Q(R29_o_p), .clk(R1_clk), .clr(R29_clear_t));
  Register #(.width(32), .trigger("falling")) RA (
    .D(multiplexer_2_out), .en(MUX_Enable), .Q(Output_A), .clk(R1_clk));  // open: clr
  Register #(.width(32), .trigger("falling")) register_21 (
    .D(Input_Data), .en(R6_en), .Q(R6_o_p), .clk(R1_clk), .clr(R6_clear_t));
  Register #(.width(32), .trigger("falling")) register_22 (
    .D(Input_Data), .en(R14_en), .Q(R14_o_p), .clk(R1_clk), .clr(R14_clear_t));
  Register #(.width(32), .trigger("falling")) register_23 (
    .D(Input_Data), .en(R22_en), .Q(R22_o_p), .clk(R1_clk), .clr(R22_clear_t));
  Register #(.width(32), .trigger("falling")) register_24 (
    .D(Input_Data), .en(R30_en), .Q(R30_o_p), .clk(R1_clk), .clr(R30_clear_t));
  Multiplexer #(.select(5), .width(32)) multiplexer_2 (
    .in0(R1_o_p), .in1(R2_o_p), .in2(R3_o_p), .in3(R4_o_p), .in4(R5_o_p), .in5(R6_o_p), .in6(R7_o_p),
    .in7(R8_o_p), .in8(R9_o_p), .in9(R10_o_p), .in10(undriven), .in11(R12_o_p), .in12(R13_o_p),
    .in13(R14_o_p), .in14(R15_o_p), .in15(R16_o_p), .in16(R17_o_p), .in17(R18_o_p), .in18(R19_o_p),
    .in19(R20_o_p), .in20(R21_o_p), .in21(R22_o_p), .in22(R23_o_p), .in23(R24_o_p), .in24(R25_o_p),
    .in25(R26_o_p), .in26(R27_o_p), .in27(R28_o_p), .in28(R29_o_p), .in29(R30_o_p), .in30(R31_o_p),
    .in31(R32_o_p), .out(multiplexer_2_out), .sel(Address_A), .en(MUX_Enable));
  Demultiplexer #(.select(5), .enable("false")) demultiplexer_1 (
    .out0(R1_en), .out1(R2_en), .out2(R3_en), .out3(R4_en), .out4(R5_en), .out5(R6_en), .out6(R7_en),
    .out7(R8_en), .out8(R9_en), .out9(R10_en), .out10(R11_en), .out11(R12_en), .out12(R13_en),
    .out13(R14_en), .out14(R15_en), .out15(R16_en), .out16(R17_en), .out17(R18_en), .out18(R19_en),
    .out19(R20_en), .out20(R21_en), .out21(R22_en), .out22(R23_en), .out23(R24_en), .out24(R25_en),
    .out25(R26_en), .out26(R27_en), .out27(R28_en), .out28(R29_en), .out29(R30_en), .out30(R31_en),
    .out31(R32_en), .in(RF_write), .sel(Address_c));
  Register #(.width(32), .trigger("falling")) register_25 (
    .D(Input_Data), .en(R7_en), .Q(R7_o_p), .clk(R1_clk), .clr(R7_clear_t));
  Register #(.width(32), .trigger("falling")) register_26 (
    .D(Input_Data), .en(R15_en), .Q(R15_o_p), .clk(R1_clk), .clr(R15_clear_t));
  Register #(.width(32), .trigger("falling")) register_27 (
    .D(Input_Data), .en(R23_en), .Q(R23_o_p), .clk(R1_clk), .clr(R23_clear_t));
  Register #(.width(32), .trigger("falling")) register_28 (
    .D(Input_Data), .en(R31_en), .Q(R31_o_p), .clk(R1_clk), .clr(R31_clear_t));
  Register #(.width(32), .trigger("falling")) register_29 (
    .D(Input_Data), .en(R8_en), .Q(R8_o_p), .clk(R1_clk), .clr(R8_clear_t));
  Register #(.width(32), .trigger("falling")) register_30 (
    .D(Input_Data), .en(R16_en), .Q(R16_o_p), .clk(R1_clk), .clr(R16_clear_t));
  Register #(.width(32), .trigger("falling")) register_31 (
    .D(Input_Data), .en(R24_en), .Q(R24_o_p), .clk(R1_clk), .clr(R24_clear_t));
  Register #(.width(32), .trigger("falling")) register_32 (
    .D(Input_Data), .en(R32_en), .Q(R32_o_p), .clk(R1_clk), .clr(R32_clear_t));

  // Other names for the same wires on the sheet: Output_MUX_Enable = MUX_Enable; R1_clear = RF_clear;
  //   R2_clear = RF_clear; R3_clear = RF_clear; R4_clear = RF_clear; R5_clear = RF_clear; R6_clear = RF_clear;
  //   R7_clear = RF_clear; R8_clear = RF_clear; R9_clear = RF_clear; R10_clear = RF_clear; R11_clear = RF_clear;
  //   R12_clear = RF_clear; R13_clear = RF_clear; R14_clear = RF_clear; R15_clear = RF_clear; R16_clear = RF_clear;
  //   R17_clear = RF_clear; R18_clear = RF_clear; R19_clear = RF_clear; R20_clear = RF_clear; R21_clear = RF_clear;
  //   R22_clear = RF_clear; R23_clear = RF_clear; R24_clear = RF_clear; R25_clear = RF_clear; R26_clear = RF_clear;
  //   R27_clear = RF_clear; R28_clear = RF_clear; R29_clear = RF_clear; R30_clear = RF_clear; R31_clear = RF_clear;
  //   R32_clear = RF_clear; R1_i_p[31:0] = Input_Data; R2_i_p[31:0] = Input_Data; R3_i_p[31:0] = Input_Data;
  //   R4_i_p[31:0] = Input_Data; R5_i_p[31:0] = Input_Data; R6_i_p[31:0] = Input_Data; R7_i_p[31:0] = Input_Data;
  //   R8_i_p[31:0] = Input_Data; R9_i_p[31:0] = Input_Data; R10_i_p[31:0] = Input_Data; R11_i_p[31:0] = Input_Data;
  //   R12_i_p[31:0] = Input_Data; R13_i_p[31:0] = Input_Data; R14_i_p[31:0] = Input_Data; R15_i_p[31:0] = Input_Data;
  //   R16_i_p[31:0] = Input_Data; R17_i_p[31:0] = Input_Data; R18_i_p[31:0] = Input_Data; R19_i_p[31:0] = Input_Data;
  //   R20_i_p[31:0] = Input_Data; R21_i_p[31:0] = Input_Data; R22_i_p[31:0] = Input_Data; R23_i_p[31:0] = Input_Data;
  //   R24_i_p[31:0] = Input_Data; R25_i_p[31:0] = Input_Data; R26_i_p[31:0] = Input_Data; R27_i_p[31:0] = Input_Data;
  //   R28_i_p[31:0] = Input_Data; R29_i_p[31:0] = Input_Data; R30_i_p[31:0] = Input_Data; R31_i_p[31:0] = Input_Data;
  //   R32_i_p[31:0] = Input_Data; R2_clk = R1_clk; R3_clk = R1_clk; R4_clk = R1_clk; R5_clk = R1_clk; R6_clk = R1_clk;
  //   R7_clk = R1_clk; R8_clk = R1_clk; R9_clk = R1_clk; R10_clk = R1_clk; R11_clk = R1_clk; R12_clk = R1_clk;
  //   R13_clk = R1_clk; R14_clk = R1_clk; R15_clk = R1_clk; R16_clk = R1_clk; R17_clk = R1_clk; R18_clk = R1_clk;
  //   R19_clk = R1_clk; R20_clk = R1_clk; R21_clk = R1_clk; R22_clk = R1_clk; R23_clk = R1_clk; R24_clk = R1_clk;
  //   R25_clk = R1_clk; R26_clk = R1_clk; R27_clk = R1_clk; R28_clk = R1_clk; R29_clk = R1_clk; R30_clk = R1_clk;
  //   R31_clk = R1_clk; R32_clk = R1_clk; RA_RB_clock = R1_clk
endmodule

module ALU (
  input  [31:0] Input_A,
  input  [31:0] Input_B,
  input  [5:0] Op_Code,
  input  ALU_MUX_Enable,
  output [31:0] ALU_Output
);

  wire clock_1_out;
  wire [3:0] bitselector_1_out;
  wire [31:0] adder_1_out, AND_out, multiplexer_1_out, OR_out, subtractor_1_out;

  Adder #(.width(32)) adder_1 (.a(Input_A), .b(Input_B), .out(adder_1_out));  // open: cin, cout
  Subtractor #(.width(32)) subtractor_1 (.a(Input_A), .b(Input_B), .out(subtractor_1_out));  // open: bin, bout
  assign AND_out = Input_A & Input_B;  // AND_Gate AND, 32 bits wide
  assign OR_out = Input_A | Input_B;  // OR_Gate OR, 32 bits wide
  BitSelector #(.width(6), .group(4)) bitselector_1 (.in(Op_Code), .out(bitselector_1_out), .sel(1'b0));
  Multiplexer #(.select(4), .width(32)) multiplexer_1 (
    .in0(Input_A), .in1(Input_B), .in2(adder_1_out), .in3(adder_1_out), .in4(subtractor_1_out),
    .in5(subtractor_1_out), .in6(AND_out), .in7(AND_out), .in8(OR_out), .in9(OR_out), .in10(adder_1_out),
    .in11(adder_1_out), .in12({32{1'b0}}), .in13({32{1'b0}}), .in14({32{1'b0}}), .in15({32{1'b0}}),
    .out(multiplexer_1_out), .sel(bitselector_1_out), .en(ALU_MUX_Enable));
  Register #(.width(32), .trigger("falling")) RZ (
    .D(multiplexer_1_out), .en(ALU_MUX_Enable), .Q(ALU_Output), .clk(clock_1_out));  // open: clr
  Clock clock_1 (.out(clock_1_out));
endmodule

module Memory (
  input  [31:0] Memory_Address,
  input  [31:0] Memory,
  input  Mem_Reset,
  input  Chip_Sel,
  input  clk,
  input  Mem_Read_Write,
  output [31:0] Data
);

  wire not_1_out, not_2_out;
  wire [23:0] bitselector_1_out;

  BitSelector #(.width(32), .group(24)) bitselector_1 (.in(Memory_Address), .out(bitselector_1_out), .sel(1'b0));
  RAM #(.addrWidth(24), .dataWidth(32), .bus("separate")) ram_1 (
    .addr(bitselector_1_out), .din(Memory), .data(Data), .str(Mem_Read_Write), .sel(Chip_Sel),
    .clk(not_2_out), .ld(not_1_out), .clr(Mem_Reset));
  not not_1 (not_1_out, Mem_Read_Write);
  not not_2 (not_2_out, clk);
endmodule

module ID (
  input  [31:0] Instruction,
  output [31:0] Immediate_Value,
  output [4:0] Source_1,
  output [4:0] Destination,
  output [5:0] Op_Code,
  output [4:0] Source_2
);

  wire comparator_1_eq;

  Comparator #(.width(6)) comparator_1 (.a(Instruction[31:26]), .b(6'b001011), .eq(comparator_1_eq));  // open: gt, lt
  Multiplexer #(.width(5), .enable("false")) multiplexer_1 (
    .in0(Instruction[15:11]), .in1(Instruction[25:21]), .out(Source_2), .sel(comparator_1_eq));
  assign Immediate_Value = {{16{1'b0}}, Instruction[15:0]};  // Bit_Extender bit_extender_1

  assign Destination = Instruction[25:21];
  assign Op_Code = Instruction[31:26];
  assign Source_1 = Instruction[20:16];
endmodule
